// Logisim project D1.circ as structural Verilog: 1 circuit, main circuit main
module main (
  input  in_1,
  input  in_2,
  output out_3,
  output out_4
);

  wire clock_1_out;

  Clock clock_1 (.out(clock_1_out));
  D_Flip_Flop d_ff_1 (.clk(in_1), .D(clock_1_out), .Q(out_3), .Qn(out_4), .en(in_2));  // open: preset, reset
endmodule
