// Logisim project Değil Kapısı.circ as structural Verilog: 2 circuits, main circuit main
module main (
  input  in_1,
  output out_2
);

  not not_1 (out_2, in_1);
endmodule

module \Değil_Kapısı  (
  input  A,
  output Q
);

  not not_1 (Q, A);
endmodule
