// Logisim project J-K.circ as structural Verilog
module J_K (
  input  Q,
  input  J,
  input  K,
  output A
);

  wire and_1_out, and_2_out, not_1_out, not_2_out;

  not not_1 (not_1_out, Q);
  not not_2 (not_2_out, K);
  and and_1 (and_1_out, not_1_out, J);
  and and_2 (and_2_out, Q, not_2_out);
  or or_1 (A, and_1_out, and_2_out);
endmodule
