// Logisim project Karşılaştırıcı.circ as structural Verilog: 1 circuit, main circuit main
module main (
  input  A,
  input  B,
  output A__B,
  output A_B
);

  xor xor_1 (A__B, A, B);
  xnor xnor_1 (A_B, A, B);
endmodule
