// Logisim project R-S.circ as structural Verilog
module R_S (
  input  R,
  input  S,
  input  Q,
  output A
);

  wire and_1_out, not_1_out;

  not not_1 (not_1_out, Q);
  and and_1 (and_1_out, R, not_1_out);
  or or_1 (A, S, and_1_out);
endmodule
