// Logisim project T_flipflop.circ as structural Verilog: 1 circuit, main circuit main
module main (
  input  in_1,
  output out_2,
  output out_3
);

  wire clock_1_out;

  Clock clock_1 (.out(clock_1_out));
  T_Flip_Flop t_ff_1 (.clk(in_1), .Q(out_2), .Qn(out_3), .en(clock_1_out));  // open: T, preset, reset
endmodule
