// Logisim project Tam_çıkarıcı.circ as structural Verilog: 1 circuit, main circuit main
module main (
  input  Bin,
  input  A,
  input  B,
  output D,
  output Bo
);

  wire and_1_out, and_2_out, not_1_out, not_2_out, xor_1_out;

  xor xor_1 (xor_1_out, A, B);
  not not_1 (not_1_out, A);
  and and_1 (and_1_out, not_1_out, B);
  not not_2 (not_2_out, xor_1_out);
  xor xor_2 (D, Bin, xor_1_out);
  and and_2 (and_2_out, Bin, not_2_out);
  or or_1 (Bo, and_2_out, and_1_out);

  // Notes on the sheet:
  //   TAM ÇIKARICI DEVRESİ
endmodule
