// Logisim project Ve Değil Kapısı.circ as structural Verilog: 2 circuits, main circuit main
module main (
  input  in_1,
  input  in_2,
  output out_3
);

  wire and_1_out;

  and and_1 (and_1_out, in_1, in_2);
  not not_1 (out_3, and_1_out);
endmodule

module \Ve_Değil_Kapısı  (
  input  A,
  input  B,
  output Q
);

  wire not_1_out, not_2_out;

  not not_1 (not_1_out, A);
  not not_2 (not_2_out, B);
  or or_1 (Q, not_1_out, not_2_out);
endmodule
