// Logisim project Veya Değil Kapısı.circ as structural Verilog
module \Veya_Değil_Kapısı  (
  input  A,
  input  B,
  output Q
);

  wire not_1_out, not_2_out;

  not not_1 (not_1_out, A);
  not not_2 (not_2_out, B);
  and and_1 (Q, not_1_out, not_2_out);
endmodule
