// Logisim project Yarım_toplayıcı.circ as structural Verilog: 1 circuit, main circuit main
module main (
  input  A,
  input  A_2,
  input  B,
  input  B_2,
  input  A_3,
  input  B_3,
  input  A_4,
  input  B_4,
  output S,
  output out_10,
  output C,
  output C_A_B
);

  wire and_1_out, and_3_out, not_1_out, not_2_out;

  not not_1 (not_1_out, B);
  and and_1 (and_1_out, A, not_1_out);
  not not_2 (not_2_out, A_3);
  and and_2 (C_A_B, A_4, B_4);
  and and_3 (and_3_out, not_2_out, B_3);
  or or_1 (out_10, and_1_out, and_3_out);
  xor xor_1 (S, A_2, B_2);
  and and_4 (C, A_2, B_2);

  // Notes on the sheet:
  //   Elde
  //   Toplam
  //   S=AB'+A'B
  //   YARIM TOPLAYICI DEVRESİ LOJİK ŞEMALARI
  //   Toplam
  //   Elde
endmodule
