// Logisim project Yarımtoplayıcıdantamtoplayıcı.circ as structural Verilog: 2 circuits, main circuit FSF
module main (
  input  A,
  input  B,
  output S,
  output C
);

  xor xor_1 (S, A, B);
  and and_1 (C, A, B);

  // Notes on the sheet:
  //   Toplam
  //   Elde
endmodule

module FSF (
  input  A,
  input  B,
  input  C,
  output out_4,
  output out_5
);

  wire main_1_c, main_1_s, main_2_c;

  main main_1 (.A(B), .B(A), .S(main_1_s), .C(main_1_c));
  and and_1 (out_4, main_1_c, main_2_c);
  main main_2 (.A(C), .B(main_1_s), .S(out_5), .C(main_2_c));

  // Notes on the sheet:
  //   Yarım toplayıcı
  //   Bir tam toplayıcıyı iki adet yarım toplayıcı ile elde etmek mümkündür.
  //   Yarım toplayıcı
endmodule
