// Logisim project Yarımçıkarıcı_örnek_69.circ as structural Verilog: 1 circuit, main circuit main
module main (
  input  A,
  input  B,
  input  in_3,
  input  in_4,
  output FARK,
  output FARK_2,
  output \BORÇ ,
  output \BORÇ_2 
);

  wire and_1_out, and_2_out, not_1_out, not_2_out, not_3_out;

  not not_1 (not_1_out, A);
  not not_2 (not_2_out, B);
  and and_1 (and_1_out, not_1_out, B);
  and and_2 (and_2_out, A, not_2_out);
  and and_3 (\BORÇ_2 , not_1_out, B);
  or or_1 (FARK_2, and_1_out, and_2_out);
  not not_3 (not_3_out, in_3);
  and and_4 (\BORÇ , in_4, not_3_out);
  xor xor_1 (FARK, in_3, in_4);

  // Notes on the sheet:
  //   YARIM ÇIKARICI LOJİK DEVRELERİ
endmodule
