// Logisim project ornek_1.circ as structural Verilog: 1 circuit, main circuit main
module main (
  input  A,
  input  B,
  input  C,
  input  D,
  input  A_2,
  input  B_2,
  input  C_2,
  input  D_2,
  input  A_3,
  input  B_3,
  input  C_3,
  input  D_3,
  input  A_4,
  input  B_4,
  input  C_4,
  input  D_4,
  output out_17
);

  wire and_1_out, and_2_out, and_3_out, and_4_out, and_5_out, not_1_out, not_2_out, not_3_out, not_4_out,
       not_5_out, not_6_out, not_7_out, not_8_out, not_9_out;

  not not_1 (not_1_out, A_2);
  not not_2 (not_2_out, C_2);
  not not_3 (not_3_out, A_3);
  not not_4 (not_4_out, B_3);
  not not_5 (not_5_out, A_4);
  not not_6 (not_6_out, C_4);
  and and_1 (and_1_out, A, B, C, D);
  and and_2 (and_2_out, not_1_out, B_2, not_2_out, D_2);
  and and_3 (and_3_out, not_3_out, not_4_out, C_3, D_3);
  and and_4 (and_4_out, not_5_out, B_4, not_6_out, D_4);
  not not_7 (not_7_out, and_2_out);
  not not_8 (not_8_out, and_3_out);
  not not_9 (not_9_out, and_4_out);
  and and_5 (and_5_out, and_1_out, not_7_out, not_8_out, not_9_out);
  not not_10 (out_17, and_5_out);

  // Notes on the sheet:
  //   A'
  //   C'
  //   A'
  //   B'
  //   A'
  //   C'
  //   (A'.B'.C'.D')'
  //   (A'.B.C'.D)'
  //   (A'.B'.C.D)'
  //   (A'.B.C'.D)'
  //   ((A'.B'.C'.D')'.(A'.B.C'.D')'.(A'.B'.C.D')'.(A'.B.C'.D)')'
endmodule
