// Logisim project ornek_10.circ as structural Verilog: 1 circuit, main circuit main
module main (
  input  B,
  input  C,
  input  D,
  input  A,
  input  C_2,
  input  D_2,
  input  A_2,
  input  B_2,
  input  C_3,
  output out_10
);

  wire nand_1_out, nand_2_out, nand_3_out, nand_4_out, nand_5_out, nand_6_out, nand_7_out;

  nand nand_1 (nand_1_out, C, C, C);
  nand nand_2 (nand_2_out, D, D);
  nand nand_3 (nand_3_out, C_2, C_2);
  nand nand_4 (nand_4_out, D_2, D_2);
  nand nand_5 (nand_5_out, B, nand_1_out, nand_2_out);
  nand nand_6 (nand_6_out, A, nand_3_out, nand_4_out);
  nand nand_7 (nand_7_out, A_2, B_2, C_3);
  nand nand_8 (out_10, nand_5_out, nand_6_out, nand_7_out);

  // Notes on the sheet:
  //   C'
  //   D'
  //   C'
  //   D'
  //   (B.C'.D')'
  //   (A.C'.D')'
  //   (A.B.C)'
  //   ((B.C'.D')'.(A.C'.D')'.(A.B.C)')'
endmodule
