// Logisim project ornek_11.circ as structural Verilog: 1 circuit, main circuit main
module main (
  input  A,
  input  B,
  input  C,
  input  D,
  input  A_2,
  input  B_2,
  input  C_2,
  input  D_2,
  input  A_3,
  input  B_3,
  input  C_3,
  input  D_3,
  input  A_4,
  input  B_4,
  input  C_4,
  input  D_4,
  input  A_5,
  input  B_5,
  input  C_5,
  input  D_5,
  output out_21
);

  wire nor_1_out, nor_2_out, nor_3_out, nor_4_out, nor_5_out, nor_6_out, nor_7_out, nor_8_out, nor_9_out,
       nor_11_out, nor_12_out, nor_13_out, nor_14_out;

  nor nor_1 (nor_1_out, C, C);
  nor nor_2 (nor_2_out, A, B, nor_1_out, nor_3_out);
  nor nor_3 (nor_3_out, D, D);
  nor nor_4 (nor_4_out, B_2, B_2);
  nor nor_5 (nor_5_out, C_2, C_2);
  nor nor_6 (nor_6_out, A_2, nor_4_out, nor_5_out, D_2);
  nor nor_7 (nor_7_out, A_3, A_3);
  nor nor_8 (nor_8_out, B_3, B_3);
  nor nor_9 (nor_9_out, nor_7_out, nor_8_out, C_3, D_3);
  nor nor_10 (out_21, nor_2_out, nor_6_out, nor_9_out, nor_11_out, nor_13_out);
  nor nor_11 (nor_11_out, A_4, B_4, C_4, D_4);
  nor nor_12 (nor_12_out, A_5, A_5);
  nor nor_13 (nor_13_out, nor_12_out, B_5, C_5, nor_14_out);
  nor nor_14 (nor_14_out, D_5, D_5);

  // Notes on the sheet:
  //   C'
  //   (A+B+C'+D')'
  //   D'
  //   B'
  //   C'
  //   (A+B'+C'+D)'
  //   A'
  //   B'
  //   (A'+B'+C+D)'
  //   ((A+B+C'+D')'+(A+B'+C'+D)'+(A'+B'+C+D)'+(A+B+C+D)'+(A'+B+C+D')')'
  //   (A+B+C+D)'
  //   A'
  //   (A'+B+C+D')'
  //   D'
endmodule
