// Logisim project ornek_12.circ as structural Verilog: 1 circuit, main circuit main
module main (
  input  K,
  input  S,
  input  Y,
  output out_4
);

  wire nor_1_out, nor_2_out, nor_3_out, nor_4_out, nor_5_out, nor_6_out, nor_7_out, nor_8_out, nor_9_out,
       nor_10_out, nor_11_out, nor_12_out, nor_13_out, nor_14_out, nor_15_out, nor_16_out, nor_17_out;

  nor nor_1 (nor_1_out, K, K);
  nor nor_2 (nor_2_out, S, S);
  nor nor_3 (nor_3_out, Y, Y);
  nor nor_4 (nor_4_out, nor_1_out, nor_1_out);
  nor nor_5 (nor_5_out, nor_2_out, nor_2_out);
  nor nor_6 (nor_6_out, nor_3_out, nor_3_out);
  nor nor_7 (nor_7_out, S, S);
  nor nor_8 (nor_8_out, Y, Y);
  nor nor_9 (nor_9_out, K, K);
  nor nor_10 (nor_10_out, Y, Y);
  nor nor_11 (nor_11_out, K, K);
  nor nor_12 (nor_12_out, S, S);
  nor nor_13 (nor_13_out, nor_4_out, nor_5_out, nor_6_out);
  nor nor_14 (nor_14_out, nor_7_out, nor_8_out);
  nor nor_15 (nor_15_out, nor_9_out, nor_10_out);
  nor nor_16 (nor_16_out, nor_11_out, nor_12_out);
  nor nor_17 (nor_17_out, nor_13_out, nor_14_out, nor_15_out, nor_16_out);
  nor nor_18 (out_4, nor_17_out, nor_17_out);

  // Notes on the sheet:
  //   HATALI İSE 1 YANAR.
endmodule
