// Logisim project ornek_13.circ as structural Verilog: 1 circuit, main circuit main
module main (
  input  in_1,
  input  in_2,
  input  in_3,
  input  in_4,
  input  in_5,
  input  in_6,
  input  in_7,
  input  in_8,
  input  in_9,
  input  in_10,
  input  in_11,
  input  in_12,
  input  in_13,
  input  in_14,
  output out_15,
  output out_16
);

  wire multiplexer_1_out, multiplexer_2_out, multiplexer_3_out, multiplexer_4_out;

  Multiplexer multiplexer_1 (.in0(in_1), .in1(in_2), .out(multiplexer_1_out), .sel(in_3));  // open: en
  Multiplexer multiplexer_2 (.in0(in_4), .in1(in_5), .out(multiplexer_2_out), .sel(in_7));  // open: en
  Multiplexer multiplexer_3 (.in0(in_8), .in1(in_9), .out(multiplexer_3_out), .sel(in_10));  // open: en
  Multiplexer multiplexer_4 (.in0(in_11), .in1(in_12), .out(multiplexer_4_out), .sel(in_14));  // open: en
  Multiplexer multiplexer_5 (.in0(multiplexer_1_out), .in1(multiplexer_2_out), .out(out_15), .sel(in_6));  // open: en
  Multiplexer multiplexer_6 (.in0(multiplexer_3_out), .in1(multiplexer_4_out), .out(out_16), .sel(in_13));  // open: en

  // Notes on the sheet:
  //   4x1
  //   4x1
endmodule
