// Logisim project ornek_14.circ as structural Verilog: 1 circuit, main circuit main
module main (
  input  I0_D_prime,
  input  I1_0,
  input  I2_0,
  input  in_4,
  input  I4_1,
  input  I5_0,
  input  I6_D_prime,
  input  I7_D_prime,
  input  [2:0] A_B_C
);

  wire multiplexer_1_out;

  Multiplexer #(.select(3)) multiplexer_1 (
    .in0(I0_D_prime), .in1(I1_0), .in2(I2_0), .in3(in_4), .in4(I4_1), .in5(I5_0), .in6(I6_D_prime),
    .in7(I7_D_prime), .out(multiplexer_1_out), .sel(A_B_C));  // open: en
  LED led_1 (.in(multiplexer_1_out));

  // Notes on the sheet:
  //   I3=D'
  //   f
endmodule
