// Logisim project ornek_15.circ as structural Verilog: 2 circuits, main circuit main
module main (
  input  in_1,
  input  in_2,
  input  in_3,
  output out_4,
  output out_5
);

  wire and_1_out, and_2_out, xor_1_out;

  xor xor_1 (xor_1_out, in_1, in_2);
  and and_1 (and_1_out, xor_1_out, in_3);
  and and_2 (and_2_out, in_1, in_2);
  xor xor_2 (out_4, xor_1_out, in_3);
  or or_1 (out_5, and_1_out, and_2_out);
endmodule

module \toplayıcı  (
  input  Cin,
  input  B0,
  input  A0,
  input  B1,
  input  A1,
  input  B2,
  input  A2,
  input  B3,
  input  A3,
  output Cout,
  output out_11,
  output out_12,
  output out_13,
  output out_14
);

  wire main_1_out_4, main_2_out_4, main_3_out_4;

  main main_1 (.in_1(A0), .in_2(B0), .in_3(Cin), .out_4(main_1_out_4), .out_5(out_11));
  main main_2 (.in_1(A1), .in_2(B1), .in_3(main_1_out_4), .out_4(main_2_out_4), .out_5(out_12));
  main main_3 (.in_1(A2), .in_2(B2), .in_3(main_2_out_4), .out_4(main_3_out_4), .out_5(out_13));
  main main_4 (.in_1(A3), .in_2(B3), .in_3(main_3_out_4), .out_4(Cout), .out_5(out_14));

  // Notes on the sheet:
  //   Cin
  //   Cin
endmodule
