// Logisim project ornek_16.circ as structural Verilog: 1 circuit, main circuit main
module main (
  input  in_1,
  input  in_2,
  input  in_3,
  input  in_4,
  input  in_5,
  input  in_6,
  input  in_7,
  input  in_8,
  input  in_9,
  input  in_10,
  input  in_11,
  input  in_12,
  input  in_13,
  input  in_14,
  input  in_15,
  input  in_16,
  input  in_17,
  input  in_18,
  output out_19,
  output out_20
);

  wire and_1_out, and_2_out, and_3_out, clock_1_out, or_1_out, or_2_out, or_3_out, or_4_out, or_5_out;

  and and_1 (and_1_out, in_1, in_2, in_3);
  and and_2 (and_2_out, in_4, in_5, in_6);
  and and_3 (and_3_out, in_7, in_8, in_9);
  or or_1 (or_1_out, and_1_out, and_2_out, and_3_out);
  or or_2 (or_2_out, in_10, in_11, in_12);
  or or_3 (or_3_out, in_13, in_14, in_15);
  or or_4 (or_4_out, in_16, in_17, in_18);
  or or_5 (or_5_out, or_2_out, or_3_out, or_4_out);
  Clock clock_1 (.out(clock_1_out));
  J_K_Flip_Flop j_k_ff_1 (
    .J(or_1_out), .clk(clock_1_out), .K(or_5_out), .Q(out_19), .Qn(out_20));  // open: preset, en, reset
endmodule
