// Logisim project ornek_2.circ as structural Verilog
module \Örnek_58  (
  input  A,
  input  B,
  input  C,
  output y
);

  wire and_1_out, and_2_out, not_1_out;

  not not_1 (not_1_out, A);
  and and_1 (and_1_out, not_1_out, C);
  and and_2 (and_2_out, A, B);
  or or_1 (y, and_1_out, and_2_out);
endmodule
