// Logisim project ornek_4.circ as structural Verilog
module \Örnek_67  (
  input  A,
  input  B,
  input  C,
  output Q
);

  wire and_1_out, and_2_out, and_3_out;

  and and_1 (and_1_out, B, C);
  and and_2 (and_2_out, A, C);
  and and_3 (and_3_out, A, B);
  or or_1 (Q, and_1_out, and_2_out, and_3_out);
endmodule
