// Logisim project ornek_6.circ as structural Verilog: 1 circuit, main circuit main
module main (
  input  A,
  input  B,
  input  C,
  input  A_2,
  input  B_2,
  input  C_2,
  input  A_3,
  input  B_3,
  input  C_3,
  output out_10
);

  wire not_1_out, not_2_out, not_3_out, not_4_out, not_5_out, not_6_out, not_7_out, not_8_out, or_1_out,
       or_2_out, or_3_out, or_4_out;

  not not_1 (not_1_out, B);
  not not_2 (not_2_out, C);
  not not_3 (not_3_out, A_2);
  not not_4 (not_4_out, B_2);
  not not_5 (not_5_out, A_3);
  or or_1 (or_1_out, A, not_1_out, not_2_out);
  or or_2 (or_2_out, not_3_out, not_4_out, C_2);
  or or_3 (or_3_out, not_5_out, B_3, C_3);
  not not_6 (not_6_out, or_1_out);
  not not_7 (not_7_out, or_2_out);
  not not_8 (not_8_out, or_3_out);
  or or_4 (or_4_out, not_6_out, not_7_out, not_8_out);
  not not_9 (out_10, or_4_out);

  // Notes on the sheet:
  //   B'
  //   C'
  //   A'
  //   B'
  //   A'
  //   (A+B'+C')'
  //   (A'+B'+C)'
  //   (A'+B+C)'
  //   ((A+B'+C')'+(A'+B'+C)'+(A'+B+C)')'
endmodule
