// Logisim project ornek_7.circ as structural Verilog: 1 circuit, main circuit main
module main (
  input  A,
  input  B,
  input  C,
  input  A_2,
  input  B_2,
  input  C_2,
  input  A_3,
  input  B_3,
  input  C_3,
  output out_10
);

  wire nand_1_out, nand_2_out, nand_3_out, nand_4_out, nand_5_out;

  nand nand_1 (nand_1_out, B, B);
  nand nand_2 (nand_2_out, C_2, C_2);
  nand nand_3 (nand_3_out, A_2, B_2, nand_2_out);
  nand nand_4 (nand_4_out, A, nand_1_out, C);
  nand nand_5 (nand_5_out, A_3, B_3, C_3);
  nand nand_6 (out_10, nand_4_out, nand_3_out, nand_5_out);

  // Notes on the sheet:
  //   C'
  //   B'
  //   (A.B.C')'
  //   (A.B.C)'
  //   (A.B'.C)'
  //   ((A.B'.C)'.(A.B.C')'.(A.B.C)')'
endmodule
