// Logisim project ornek_8.circ as structural Verilog: 1 circuit, main circuit main
module main (
  input  A,
  input  B,
  input  C,
  input  D,
  output out_5
);

  wire nor_1_out, nor_2_out, nor_3_out, nor_4_out, nor_5_out, nor_6_out, nor_7_out, nor_8_out, nor_9_out,
       nor_10_out, nor_11_out, nor_12_out, nor_13_out, nor_14_out, nor_15_out, nor_16_out, nor_17_out,
       nor_18_out, nor_19_out, nor_20_out, nor_21_out, nor_22_out, nor_23_out, nor_24_out, nor_25_out,
       nor_26_out, nor_27_out, nor_28_out, nor_29_out, nor_30_out, nor_31_out, nor_32_out, nor_33_out,
       nor_34_out, nor_35_out, nor_36_out, nor_37_out;

  not nor_1 (nor_1_out, D);  // NOR_Gate
  not nor_2 (nor_2_out, A);  // NOR_Gate
  not nor_3 (nor_3_out, C);  // NOR_Gate
  not nor_4 (nor_4_out, B);  // NOR_Gate
  not nor_5 (nor_5_out, C);  // NOR_Gate
  not nor_6 (nor_6_out, nor_1_out);  // NOR_Gate
  not nor_7 (nor_7_out, nor_2_out);  // NOR_Gate
  not nor_8 (nor_8_out, nor_3_out);  // NOR_Gate
  not nor_9 (nor_9_out, nor_4_out);  // NOR_Gate
  not nor_10 (nor_10_out, nor_5_out);  // NOR_Gate
  nor nor_11 (nor_11_out, nor_6_out, nor_6_out);
  nor nor_12 (nor_12_out, nor_7_out, nor_7_out);
  nor nor_13 (nor_13_out, nor_8_out, nor_8_out);
  nor nor_14 (nor_14_out, nor_9_out, nor_9_out);
  nor nor_15 (nor_15_out, nor_10_out, nor_10_out);
  nor nor_16 (nor_16_out, A, A);
  nor nor_17 (nor_17_out, B, B);
  nor nor_18 (nor_18_out, C, C);
  nor nor_19 (nor_19_out, nor_11_out, nor_11_out);
  nor nor_20 (nor_20_out, nor_12_out, nor_12_out);
  nor nor_21 (nor_21_out, B, B);
  nor nor_22 (nor_22_out, nor_13_out, nor_13_out);
  nor nor_23 (nor_23_out, D, D);
  nor nor_24 (nor_24_out, A, A);
  nor nor_25 (nor_25_out, nor_14_out, nor_14_out);
  nor nor_26 (nor_26_out, nor_15_out, nor_15_out);
  nor nor_27 (nor_27_out, D, D);
  nor nor_28 (nor_28_out, nor_16_out, nor_17_out, nor_18_out, nor_19_out);
  nor nor_29 (nor_29_out, nor_20_out, nor_21_out, nor_22_out, nor_23_out);
  nor nor_30 (nor_30_out, nor_24_out, nor_25_out, nor_26_out, nor_27_out);
  nor nor_31 (nor_31_out, nor_28_out, nor_28_out);
  nor nor_32 (nor_32_out, nor_29_out, nor_29_out);
  nor nor_33 (nor_33_out, nor_30_out, nor_30_out);
  nor nor_34 (nor_34_out, nor_31_out, nor_31_out);
  nor nor_35 (nor_35_out, nor_32_out, nor_32_out);
  nor nor_36 (nor_36_out, nor_33_out, nor_33_out);
  nor nor_37 (nor_37_out, nor_34_out, nor_35_out, nor_36_out);
  nor nor_38 (out_5, nor_37_out, nor_37_out);
endmodule
