// Logisim project ornek_9.circ as structural Verilog: 1 circuit, main circuit main
module main (
  input  _1,
  input  _2,
  input  _3,
  output out_4
);

  wire nor_1_out, nor_2_out, nor_3_out, nor_4_out, nor_5_out, nor_6_out, nor_7_out, nor_8_out, nor_9_out,
       nor_10_out, nor_11_out, nor_12_out, nor_13_out, nor_14_out, nor_15_out, nor_16_out, nor_17_out,
       nor_18_out, nor_19_out;

  nor nor_1 (nor_1_out, _1, _1);
  nor nor_2 (nor_2_out, _2, _2);
  nor nor_3 (nor_3_out, _1, _1);
  nor nor_4 (nor_4_out, _3, _3);
  nor nor_5 (nor_5_out, _2, _2);
  nor nor_6 (nor_6_out, _3, _3);
  nor nor_7 (nor_7_out, nor_3_out, nor_3_out);
  nor nor_8 (nor_8_out, _2, _2);
  nor nor_9 (nor_9_out, nor_4_out, nor_4_out);
  nor nor_10 (nor_10_out, _1, _1);
  nor nor_11 (nor_11_out, nor_5_out, nor_5_out);
  nor nor_12 (nor_12_out, nor_6_out, nor_6_out);
  nor nor_13 (nor_13_out, nor_1_out, nor_1_out);
  nor nor_14 (nor_14_out, nor_2_out, nor_2_out);
  nor nor_15 (nor_15_out, _3, _3);
  nor nor_16 (nor_16_out, nor_7_out, nor_8_out, nor_9_out);
  nor nor_17 (nor_17_out, nor_10_out, nor_11_out, nor_12_out);
  nor nor_18 (nor_18_out, nor_13_out, nor_14_out, nor_15_out);
  nor nor_19 (nor_19_out, nor_18_out, nor_16_out, nor_17_out);
  nor nor_20 (out_4, nor_19_out, nor_19_out);
endmodule
