// Logisim project Özel Veya Değil Kapısı.circ as structural Verilog
module \Özel_Veya_Değil_Kapısı  (
  input  A,
  input  B,
  output Q
);

  wire and_1_out, and_2_out, not_1_out, not_2_out;

  not not_1 (not_1_out, A);
  not not_2 (not_2_out, B);
  and and_1 (and_1_out, not_1_out, not_2_out);
  and and_2 (and_2_out, A, B);
  or or_1 (Q, and_1_out, and_2_out);
endmodule
